# Fritzing sketch PicoPCB_2023-08-24 (saved by Fritzing 1.0.3b)
circuit board: 8cm x 8cm
breadboards: 1

parts:
  R1 = Resistor [tolerance=±5% power=0.25 resistance=47 package=THT]
  Mod1 = Raspberry Pi Pico
  U1 = AD22100 - Voltage Output Temperature Sensor with Signal Conditioning [part_number=AD22100]
  WeMos_D1_Mini_Relay_Shield1 = WeMos D1 Mini Relay Shield

nets:
  N1: R1.Pin_0, R1.Pin_1, Mod1.pin_3, Mod1.pin_8, Mod1.pin_13, Mod1.pin_18, Mod1.pin_21, Mod1.pin_23, Mod1.pin_25, Mod1.pin_28, Mod1.pin_33, Mod1.pin_38, Mod1.pin_40, Mod1.pin_42, U1.V+, U1.Vo, U1.GND
  N2: Mod1.pin_20, WeMos_D1_Mini_Relay_Shield1.D1
  3V3: WeMos_D1_Mini_Relay_Shield1.3V3, WeMos_D1_Mini_Relay_Shield1.5V

notes:
  EasyPicoPCB(2023-08-24)
  Pico Greenhouse Controller
  Made with fritzing
  USB
  ! 3,3V from the Pico !
  R (Ohm) = (Vcc - Vf) / I (Amp)
  Green LED : 45  = (3,3 - 2,4) / 0.02
  Orange LED : 65  = (3,3 - 2) / 0.02
  Red LED : 85  = (3,3 - 1,6) / 0.02

custom parts:
  Raspberry Pi Pico: Raspberry Pi Pico. Based around the RP2040 microcontroller the Pico is a low cost microcontroller device bringing Raspberry Pi quality, cost, and easy of use to the microcontroller space. Jan 2021, Split part in to two versions: tht (this one) and SMD. This one will drill holes for a .1 in header in pcb to allow plugging in the module as well as providing pads to solder the module to the top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

// code stored in the sketch: EasyPicoPCB.ino

